# Fritzing sketch Untitled Sketch 2 (saved by Fritzing 0.9.3b)

parts:
  Part1 = NRF24L01+ Breakout Board
  Part3 = Arduino Uno (Rev3)
  Part4 = Arduino Uno (Rev3)
  Part5 = NRF24L01+ Breakout Board
  Part6 = NRF24L01+ Breakout Board
  U1 = ESP8266 NodeMCU LoLin module
  U2 = POT [package=pot_mammoth]
  J1 = Basic Servo
  J2 = Basic Servo

nets:
  GND: Part1.GND, Part3.GND, U2.E
  VCC: Part1.VCC, Part3.5V, U2.S
  N1: Part1.CE, Part3.D7
  N2: Part1.CS, Part3.D8
  N3: Part1.SCK, Part3.D13/SCK
  N4: Part1.MOSI, Part3.D11_PWM/MOSI
  N5: Part1.MISO, Part3.D12/MISO
  N6: Part3.A0, U2.A
  N7: Part4.D8, Part5.CS
  N8: Part4.D11_PWM/MOSI, Part5.MOSI
  N9: Part4.D12/MISO, Part5.MISO
  N10: Part4.D13/SCK, Part5.SCK
  N11: Part4.D5_PWM, J1.pulse
  N12: Part4.D7, Part5.CE
  VCC_2: Part4.5V, Part5.VCC, J1.vcc
  GND_2: Part4.GND, Part5.GND, J1.gnd
  GND_3: Part6.GND, U1.GND, J2.gnd
  VCC_3: Part6.VCC, U1.3V3, J2.vcc
  N13: Part6.CE, U1.D4
  N14: Part6.CS, U1.D2
  N15: Part6.SCK, U1.D5
  N16: Part6.MOSI, U1.D7
  N17: Part6.MISO, U1.D6
  N18: U1.D0, J2.pulse

notes:
  1.VCC|2.CSN|3.MOSI|4.IRQ
  5.GND|6.CE|7.SCK|8.MISO

custom parts:
  ESP8266 NodeMCU LoLin module: ESP8266 based NodeMCU
